// Logisim project Z1.circ as structural Verilog: 1 circuit, main circuit main
module main (
  input  [2:0] A,
  input  [2:0] B,
  output [2:0] out_3,
  output [2:0] out_4,
  output [3:0] AB,
  output [3:0] out_6
);

  wire nor_1_out, nor_2_out, nor_3_out, nor_4_out;

  nor nor_1 (nor_1_out, B[1], B[1]);
  nor nor_2 (nor_2_out, nor_1_out, A[2], A[0]);
  nor nor_3 (nor_3_out, nor_2_out, nor_4_out);
  nor nor_4 (nor_4_out, nor_1_out, B[2], B[0]);
  nor nor_5 (AB[2], nor_3_out, nor_3_out);

  assign {AB[3], AB[1:0]} = {{2{B[1]}}, 1'b0};
  assign out_3 = A;
  assign out_4 = B;
  assign out_6 = {B[1], AB[2], B[1], 1'b0};

  // Other names for the same wires on the sheet: R2 = AB[2]; R1 = B[1]; R3 = B[1]
endmodule
