// Logisim project Z2.circ as structural Verilog: 1 circuit, main circuit main
module main (
  input  [3:0] Ulaz,
  output out_2,
  output out_3,
  output out_4,
  output out_5,
  output out_6,
  output out_7,
  output out_8
);

  wire and_1_out, and_2_out, multiplexer_2_out, multiplexer_3_out, multiplexer_4_out, multiplexer_6_out,
       multiplexer_8_out, multiplexer_9_out, nand_1_out, nand_2_out, nor_1_out, nor_2_out, nor_3_out,
       nor_4_out, nor_5_out, nor_6_out, nor_7_out, nor_8_out, not_1_out, not_2_out, not_3_out;
  wire [0:0] multiplexer_7_out;

  Multiplexer #(.select(3)) multiplexer_1 (
    .in0(1'b0), .in1(1'b1), .in2(1'b1), .in3(1'b1), .in4(1'b0), .in5(1'b1), .in6(1'b1), .in7(1'b0),
    .out(out_3), .sel(Ulaz[3:1]));
  Multiplexer multiplexer_2 (.in0(1'b1), .in1(1'b0), .out(multiplexer_2_out), .sel(Ulaz[2]));
  Multiplexer multiplexer_3 (.in0(1'b1), .in1(1'b0), .out(multiplexer_3_out), .sel(Ulaz[1]));
  Multiplexer multiplexer_4 (.in0(multiplexer_2_out), .in1(1'b1), .out(multiplexer_4_out), .sel(Ulaz[3]));
  Multiplexer multiplexer_5 (.in0(multiplexer_4_out), .in1(1'b1), .out(out_2), .sel(multiplexer_6_out));
  Multiplexer multiplexer_6 (.in0(Ulaz[1]), .in1(multiplexer_3_out), .out(multiplexer_6_out), .sel(Ulaz[0]));
  not not_1 (not_1_out, Ulaz[0]);
  or or_1 (out_4, not_1_out, Ulaz[1], not_2_out);
  not not_2 (not_2_out, Ulaz[2]);
  _7_Segment_Display #(.decimalPoint("false")) DISPLEJ (
    .g(out_8), .f(out_7), .a(out_2), .b(out_3), .e(out_6), .d(out_5), .c(out_4));
  nor nor_1 (nor_1_out, Ulaz[0], Ulaz[0]);
  nor nor_2 (nor_2_out, Ulaz[3], Ulaz[3]);
  nor nor_3 (nor_3_out, Ulaz[1], Ulaz[1]);
  nand nand_1 (nand_1_out, Ulaz[2], Ulaz[1]);
  nor nor_4 (nor_4_out, nor_1_out, Ulaz[1]);
  nor nor_5 (nor_5_out, Ulaz[2], nor_1_out);
  nor nor_6 (nor_6_out, nor_2_out, Ulaz[1]);
  nor nor_7 (nor_7_out, nor_3_out, Ulaz[3], Ulaz[0]);
  nand nand_2 (nand_2_out, nand_1_out, Ulaz[0]);
  nor nor_8 (nor_8_out, nor_4_out, nor_5_out, nor_6_out, nor_7_out);
  nand nand_3 (out_6, nand_2_out, nand_2_out);
  nor nor_9 (out_5, nor_8_out, nor_8_out);
  and and_1 (and_1_out, Ulaz[1], Ulaz[0]);
  and and_2 (and_2_out, Ulaz[3], not_3_out);
  not not_3 (not_3_out, Ulaz[1]);
  or or_2 (out_7, and_1_out, and_2_out);
  Multiplexer #(.select(2)) multiplexer_7 (
    .in0(1'b1), .in1(1'b0), .out(multiplexer_7_out[0]), .sel({1'b0, Ulaz[1]}));  // open: in2, in3
  Multiplexer #(.select(2)) multiplexer_8 (
    .in0(Ulaz[0]), .out(multiplexer_8_out), .sel({1'b0, multiplexer_7_out[0]}));  // open: in1, in2, in3
  Multiplexer #(.select(2)) multiplexer_9 (
    .in0(Ulaz[1]), .in1(1'b1), .out(multiplexer_9_out), .sel({1'b0, Ulaz[0]}));  // open: in2, in3
  Multiplexer #(.select(2)) multiplexer_10 (
    .in0(1'b0), .in1(multiplexer_9_out), .in2(multiplexer_8_out), .in3(1'b1), .out(out_8), .sel(Ulaz[3:2]));

  // Other names for the same wires on the sheet: U1 = Ulaz[1]; U0 = Ulaz[0]; U2 = Ulaz[2]; U3 = Ulaz[3]; A = out_2;
  //   B = out_3; C = out_4; D = out_5; E = out_6; F = out_7; G = out_8
endmodule
