// Logisim project Z3.circ as structural Verilog: 3 circuits, main circuit main
module main (
  input  [7:0] A,
  input  [7:0] B,
  input  [1:0] in_3,
  output [7:0] out_4,
  output [7:0] out_5,
  output [7:0] Rezultat,
  output [7:0] out_7,
  output out_8
);

  wire alu_1_cout, alu_2_cout, alu_3_cout, alu_4_cout, alu_5_cout, alu_6_cout, alu_7_cout;

  ALU alu_1 (.A(A[0]), .B(B[0]), .Cin(1'b0), .S(in_3), .Cout(alu_1_cout), .Izlaz(out_7[0]));
  ALU alu_2 (.A(A[1]), .B(B[1]), .Cin(alu_1_cout), .S(in_3), .Cout(alu_2_cout), .Izlaz(out_7[1]));
  ALU alu_3 (.A(A[2]), .B(B[2]), .Cin(alu_2_cout), .S(in_3), .Cout(alu_3_cout), .Izlaz(out_7[2]));
  ALU alu_4 (.A(A[3]), .B(B[3]), .Cin(alu_3_cout), .S(in_3), .Cout(alu_4_cout), .Izlaz(out_7[3]));
  ALU alu_5 (.A(A[4]), .B(B[4]), .Cin(alu_4_cout), .S(in_3), .Cout(alu_5_cout), .Izlaz(out_7[4]));
  ALU alu_6 (.A(A[5]), .B(B[5]), .Cin(alu_5_cout), .S(in_3), .Cout(alu_6_cout), .Izlaz(out_7[5]));
  ALU alu_7 (.A(A[6]), .B(B[6]), .Cin(alu_6_cout), .S(in_3), .Cout(alu_7_cout), .Izlaz(out_7[6]));
  ALU alu_8 (.A(A[7]), .B(B[7]), .Cin(alu_7_cout), .S(in_3), .Cout(out_8), .Izlaz(out_7[7]));

  assign out_4 = A;
  assign out_5 = B;
  assign Rezultat = out_7;

  // Other names for the same wires on the sheet: Cout = out_8; R0 = out_7[0]; R1 = out_7[1]; R2 = out_7[2];
  //   R3 = out_7[3]; R4 = out_7[4]; R5 = out_7[5]; R6 = out_7[6]; R7 = out_7[7]; S[1:0] = in_3
endmodule

module Oduzimac (
  input  A,
  input  B,
  input  Cin,
  output Rezultat,
  output Cout
);

  wire and_1_out, and_2_out, and_3_out, and_4_out, and_5_out, and_6_out, and_7_out, not_1_out, not_2_out,
       not_3_out;

  not not_1 (not_1_out, A);
  not not_2 (not_2_out, B);
  not not_3 (not_3_out, Cin);
  and and_1 (and_1_out, not_1_out, not_2_out, Cin);
  and and_2 (and_2_out, not_1_out, B, not_3_out);
  and and_3 (and_3_out, A, not_2_out, not_3_out);
  and and_4 (and_4_out, A, B, Cin);
  and and_5 (and_5_out, not_1_out, Cin);
  and and_6 (and_6_out, not_1_out, B);
  and and_7 (and_7_out, B, Cin);
  or or_1 (Rezultat, and_1_out, and_2_out, and_3_out, and_4_out);
  or or_2 (Cout, and_5_out, and_6_out, and_7_out);
endmodule

module ALU (
  input  A,
  input  B,
  input  Cin,
  input  [1:0] S,
  output Cout,
  output Izlaz
);

  wire nand_1_out, nand_2_out, nand_3_out, nor_1_out, nor_2_out, nor_3_out, not_1_out, oduzimac_1_rezultat;

  not not_1 (not_1_out, A);
  nor nor_1 (nor_1_out, B, B);
  nor nor_2 (nor_2_out, A, A);
  nand nand_1 (nand_1_out, B, B);
  nand nand_2 (nand_2_out, A, A);
  Oduzimac oduzimac_1 (.A(A), .B(B), .Cin(Cin), .Rezultat(oduzimac_1_rezultat), .Cout(Cout));
  nor nor_3 (nor_3_out, nor_1_out, nor_2_out);
  nand nand_3 (nand_3_out, nand_1_out, nand_2_out);
  Multiplexer #(.select(2)) multiplexer_1 (
    .in0(oduzimac_1_rezultat), .in1(not_1_out), .in2(nor_3_out), .in3(nand_3_out), .out(Izlaz), .sel(S));
endmodule
