// Logisim project Z4.circ as structural Verilog: 2 circuits, main circuit main
module main (
  input  [7:0] A,
  input  [7:0] B,
  output [7:0] out_3,
  output [7:0] out_4
);

  wire komparator_1_m1, komparator_1_v1, komparator_2_m1, komparator_2_v1, komparator_3_m1, komparator_3_v1,
       komparator_4_m1, komparator_4_v1, komparator_5_m1, komparator_5_v1, komparator_6_m1, komparator_6_v1,
       komparator_7_m1, komparator_7_v1, manji, veci;

  komparator komparator_1 (.A(A[0]), .B(B[0]), .V(1'b0), .M(1'b0), .V1(komparator_1_v1), .M1(komparator_1_m1));
  komparator komparator_2 (
    .A(A[1]), .B(B[1]), .V(komparator_1_v1), .M(komparator_1_m1), .V1(komparator_2_v1), .M1(komparator_2_m1));
  komparator komparator_3 (
    .A(A[2]), .B(B[2]), .V(komparator_2_v1), .M(komparator_2_m1), .V1(komparator_3_v1), .M1(komparator_3_m1));
  komparator komparator_4 (
    .A(A[3]), .B(B[3]), .V(komparator_3_v1), .M(komparator_3_m1), .V1(komparator_4_v1), .M1(komparator_4_m1));
  LED led_1 (.in(veci));
  LED led_2 (.in(manji));
  komparator komparator_5 (
    .A(A[4]), .B(B[4]), .V(komparator_4_v1), .M(komparator_4_m1), .V1(komparator_5_v1), .M1(komparator_5_m1));
  komparator komparator_6 (
    .A(A[5]), .B(B[5]), .V(komparator_5_v1), .M(komparator_5_m1), .V1(komparator_6_v1), .M1(komparator_6_m1));
  komparator komparator_7 (
    .A(A[6]), .B(B[6]), .V(komparator_6_v1), .M(komparator_6_m1), .V1(komparator_7_v1), .M1(komparator_7_m1));
  komparator komparator_8 (.A(A[7]), .B(B[7]), .V(komparator_7_v1), .M(komparator_7_m1), .V1(veci), .M1(manji));

  assign out_3 = A;
  assign out_4 = B;

  // Notes on the sheet:
  //   Zelena - ON
  //   Crvena - OFF
endmodule

module komparator (
  input  A,
  input  B,
  input  V,
  input  M,
  output V1,
  output M1
);

  wire nor_1_out, nor_2_out, nor_3_out, nor_4_out, nor_5_out, nor_6_out, nor_7_out, nor_8_out, not_1_out,
       not_2_out, not_3_out, not_4_out;

  not not_1 (not_1_out, A);
  not not_2 (not_2_out, B);
  not not_3 (not_3_out, V);
  not not_4 (not_4_out, M);
  nor nor_1 (nor_1_out, B, not_3_out);
  nor nor_2 (nor_2_out, not_1_out, B);
  nor nor_3 (nor_3_out, not_1_out, not_3_out);
  nor nor_4 (nor_4_out, A, not_4_out);
  nor nor_5 (nor_5_out, A, not_2_out);
  nor nor_6 (nor_6_out, not_2_out, not_4_out);
  nor nor_7 (nor_7_out, nor_1_out, nor_2_out, nor_3_out);
  nor nor_8 (nor_8_out, nor_4_out, nor_5_out, nor_6_out);
  nor nor_9 (V1, nor_7_out, nor_7_out);
  nor nor_10 (M1, nor_8_out, nor_8_out);
endmodule
