// Logisim project Zadatak1.circ as structural Verilog
module Mealy (
  input  Ulaz,
  input  clock,
  output Rezultat
);

  wire and_1_out, and_2_out, and_3_out, and_4_out, and_5_out, and_6_out, and_7_out, and_8_out, and_9_out,
       and_10_out, and_11_out, not_1_out, not_2_out, not_3_out, not_4_out, or_1_out, or_2_out, or_3_out, q0,
       q1, q2;

  not not_1 (not_1_out, q2);
  not not_2 (not_2_out, q1);
  not not_3 (not_3_out, q0);
  not not_4 (not_4_out, Ulaz);
  and and_1 (and_1_out, q1, not_4_out);
  and and_2 (and_2_out, q2, not_3_out, Ulaz);
  and and_3 (and_3_out, q2, q0, not_4_out);
  and and_4 (and_4_out, not_1_out, q0, not_4_out);
  and and_5 (and_5_out, not_1_out, q1, not_4_out);
  and and_6 (and_6_out, q1, q0);
  and and_7 (and_7_out, q2, Ulaz);
  and and_8 (and_8_out, not_3_out, Ulaz);
  and and_9 (and_9_out, q0, not_4_out);
  and and_10 (and_10_out, q2, not_2_out);
  and and_11 (and_11_out, not_1_out, q1, not_3_out);
  and and_12 (Rezultat, q2, not_3_out, Ulaz);
  or or_1 (or_1_out, and_1_out, and_2_out, and_3_out);
  or or_2 (or_2_out, and_4_out, and_5_out, and_6_out, and_7_out);
  or or_3 (or_3_out, and_8_out, and_9_out, and_10_out, and_11_out);
  T_Flip_Flop t_ff_1 (.T(or_1_out), .clk(clock), .Q(q2));  // open: Qn, reset, preset
  T_Flip_Flop t_ff_2 (.T(or_2_out), .clk(clock), .Q(q1));  // open: Qn, reset, preset
  T_Flip_Flop t_ff_3 (.T(or_3_out), .clk(clock), .Q(q0));  // open: Qn, reset, preset
endmodule

module Moore (
  input  Ulaz,
  input  clock,
  output Rezultat
);

  wire and_1_out, and_2_out, and_3_out, and_4_out, and_5_out, and_6_out, and_7_out, and_8_out, and_9_out,
       and_10_out, and_11_out, and_12_out, and_13_out, and_14_out, not_1_out, not_2_out, not_3_out,
       not_4_out, or_1_out, or_2_out, or_3_out, or_4_out, q0, q1, q2, q3;

  not not_1 (not_1_out, q2);
  not not_2 (not_2_out, q1);
  not not_3 (not_3_out, q0);
  not not_4 (not_4_out, Ulaz);
  and and_1 (and_1_out, q2, q1, q0, Ulaz);
  and and_2 (and_2_out, q1, not_4_out);
  and and_3 (and_3_out, q2, q0, Ulaz);
  and and_4 (and_4_out, q3, not_4_out);
  and and_5 (and_5_out, not_1_out, q0, not_4_out);
  and and_6 (and_6_out, q2, not_3_out, not_4_out);
  and and_7 (and_7_out, q1, q0, Ulaz);
  and and_8 (and_8_out, not_3_out, Ulaz);
  and and_9 (and_9_out, q0, not_4_out);
  and and_10 (and_10_out, not_1_out, not_2_out, Ulaz);
  and and_11 (and_11_out, q2, not_2_out, not_3_out);
  and and_12 (and_12_out, q2, q1, Ulaz);
  and and_13 (and_13_out, q3, Ulaz);
  and and_14 (and_14_out, q2, not_2_out, q0, Ulaz);
  or or_1 (or_1_out, q3, and_1_out);
  or or_2 (or_2_out, and_2_out, and_3_out);
  or or_3 (or_3_out, and_4_out, and_5_out, and_6_out, and_7_out);
  or or_4 (or_4_out, and_8_out, and_9_out, and_10_out, and_11_out, and_12_out);
  or or_5 (Rezultat, and_13_out, and_14_out);
  T_Flip_Flop t_ff_1 (.T(or_1_out), .clk(clock), .Q(q3));  // open: Qn, reset, preset
  T_Flip_Flop t_ff_2 (.T(or_2_out), .clk(clock), .Q(q2));  // open: Qn, reset, preset
  T_Flip_Flop t_ff_3 (.T(or_3_out), .clk(clock), .Q(q1));  // open: Qn, reset, preset
  T_Flip_Flop t_ff_4 (.T(or_4_out), .clk(clock), .Q(q0));  // open: Qn, reset, preset
endmodule

module Zad1 (
  input  Ulaz,
  output Rezultat1,
  output Rezultat2
);

  wire clock_1_out;

  Clock clock_1 (.out(clock_1_out));
  Mealy mealy_1 (.Ulaz(Ulaz), .clock(clock_1_out), .Rezultat(Rezultat1));
  Moore moore_1 (.Ulaz(Ulaz), .clock(clock_1_out), .Rezultat(Rezultat2));
endmodule
