// Logisim project Zadatak2.circ as structural Verilog
module BrojacMod16 (
  input  clock,
  output [3:0] Rezultat
);

  wire and_1_out, and_2_out;

  and and_1 (and_1_out, Rezultat[2], Rezultat[1], Rezultat[0]);
  and and_2 (and_2_out, Rezultat[1], Rezultat[0]);
  T_Flip_Flop t_ff_1 (.T(and_1_out), .clk(clock), .Q(Rezultat[3]));  // open: Qn, reset, preset
  T_Flip_Flop t_ff_2 (.T(and_2_out), .clk(clock), .Q(Rezultat[2]));  // open: Qn, reset, preset
  T_Flip_Flop t_ff_3 (.T(Rezultat[0]), .clk(clock), .Q(Rezultat[1]));  // open: Qn, reset, preset
  T_Flip_Flop t_ff_4 (.T(1'b1), .clk(clock), .Q(Rezultat[0]));  // open: Qn, reset, preset

  // Other names for the same wires on the sheet: q0 = Rezultat[0]; q1 = Rezultat[1]; q2 = Rezultat[2];
  //   q3 = Rezultat[3]
endmodule

module CMP1bit (
  input  A,
  input  B,
  input  Vin,
  input  Min,
  input  Jin,
  output Vout,
  output Mout,
  output Jout
);

  wire nor_1_out, nor_2_out, nor_3_out, nor_4_out, nor_5_out, nor_6_out, nor_7_out, nor_8_out, nor_9_out,
       nor_10_out, nor_11_out;

  nor nor_1 (nor_1_out, A, A);
  nor nor_2 (nor_2_out, B, B);
  nor nor_3 (nor_3_out, nor_1_out, B);
  nor nor_4 (nor_4_out, A, nor_2_out);
  nor nor_5 (nor_5_out, nor_3_out, nor_3_out);
  nor nor_6 (nor_6_out, nor_4_out, nor_4_out);
  nor nor_7 (nor_7_out, Jin, Jin);
  nor nor_8 (nor_8_out, nor_5_out, nor_7_out);
  nor nor_9 (nor_9_out, nor_7_out, nor_6_out);
  nor nor_10 (nor_10_out, nor_8_out, Vin);
  nor nor_11 (nor_11_out, Min, nor_9_out);
  nor nor_12 (Vout, nor_10_out, nor_10_out);
  nor nor_13 (Mout, nor_11_out, nor_11_out);
  nor nor_14 (Jout, Mout, Vout);
endmodule

module CMP4bit (
  input  [3:0] A,
  input  [3:0] B,
  output Izlaz
);

  wire cmp1bit_1_jout, cmp1bit_1_mout, cmp1bit_1_vout, cmp1bit_2_jout, cmp1bit_2_mout, cmp1bit_2_vout,
       cmp1bit_3_jout, cmp1bit_3_mout, cmp1bit_3_vout;

  CMP1bit cmp1bit_1 (
    .A(A[3]), .B(B[3]), .Vin(1'b0), .Min(1'b0), .Jin(1'b1), .Vout(cmp1bit_1_vout), .Mout(cmp1bit_1_mout),
    .Jout(cmp1bit_1_jout));
  CMP1bit cmp1bit_2 (
    .A(A[2]), .B(B[2]), .Vin(cmp1bit_1_vout), .Min(cmp1bit_1_mout), .Jin(cmp1bit_1_jout),
    .Vout(cmp1bit_2_vout), .Mout(cmp1bit_2_mout), .Jout(cmp1bit_2_jout));
  CMP1bit cmp1bit_3 (
    .A(A[1]), .B(B[1]), .Vin(cmp1bit_2_vout), .Min(cmp1bit_2_mout), .Jin(cmp1bit_2_jout),
    .Vout(cmp1bit_3_vout), .Mout(cmp1bit_3_mout), .Jout(cmp1bit_3_jout));
  CMP1bit cmp1bit_4 (
    .A(A[0]), .B(B[0]), .Vin(cmp1bit_3_vout), .Min(cmp1bit_3_mout), .Jin(cmp1bit_3_jout), .Mout(Izlaz));  // open: Vout, Jout
endmodule

module Zad2 (
  input  Ulaz,
  output [3:0] out_2,
  output Rezultat,
  output [3:0] out_4
);

  wire brojac_1_rezultat, clock_1_out, decoder_1_out0, decoder_1_out1;

  Clock clock_1 (.out(clock_1_out));
  Decoder decoder_1 (.out0(decoder_1_out0), .out1(decoder_1_out1), .sel(Ulaz), .en(brojac_1_rezultat));
  Brojac brojac_1 (.clock(clock_1_out), .Rezultat(brojac_1_rezultat));
  BrojacMod16 Brojac_Parnih (.clock(decoder_1_out0), .Rezultat(out_2));
  BrojacMod16 Brojac_Neparnih (.clock(decoder_1_out1), .Rezultat(out_4));
  CMP4bit cmp4bit_1 (.A(out_2), .B(out_4), .Izlaz(Rezultat));
endmodule

module Brojac (
  input  clock,
  output Rezultat
);

  wire not_1_out, not_2_out, or_1_out, q0, q1;

  not not_1 (not_1_out, q1);
  not not_2 (not_2_out, q0);
  or or_1 (or_1_out, not_1_out, not_2_out);
  and and_1 (Rezultat, q1, q0);
  T_Flip_Flop t_ff_1 (.T(q0), .clk(clock), .Q(q1));  // open: Qn, reset, preset
  T_Flip_Flop t_ff_2 (.T(or_1_out), .clk(clock), .Q(q0));  // open: Qn, reset, preset
endmodule
